# Fritzing sketch Sample Layout (saved by Fritzing 0.9.3b)
breadboards: 1

parts:
  Part1 = Arduino Uno (Rev3)
  VCC1 = Battery block 9V
  RHT1 = Humidity and Temperature Sensor RHT03
  S1 = SPST Switch [package=switch-spdt_lock.007s]
  Raspberry_Pi_1 = Raspberry Pi 3 [part_number=RPI-3-V1.2]
  R1 = Resistor [tolerance=±5% resistance=220 package="0603 [SMD]"]
  X1 = DB9 Connector [package=db9]
  MD03A1 = Dual VNH2SP30 Motor Driver [part_number=MD03A]
  M1 = DC Motor
  M2 = DC Motor
  hc-sr2 = hc-sr04
  hc-sr3 = hc-sr04
  hc-sr4 = hc-sr04
  hc-sr5 = hc-sr04

nets:
  N1: Part1.D12/MISO, RHT1.Vcc, R1.Pin_0
  N2: Part1.A4/SDA, Raspberry_Pi_1.GPIO2
  N3: Part1.A5/SCL, Raspberry_Pi_1.GPIO3
  N4: Part1.D0/RX, X1.3
  N5: Part1.D1/TX, X1.2
  N6: Part1.3V3, RHT1.Data-signal, R1.Pin_1
  VCC: Part1.5V, hc-sr2.VCC, hc-sr3.VCC, hc-sr4.VCC, hc-sr5.VCC
  GND: Part1.GND, VCC1.-, RHT1.GND_2, X1.5, MD03A1.GND, hc-sr2.GND, hc-sr3.GND, hc-sr4.GND, hc-sr5.GND
  VIN: Part1.VIN, S1.P, MD03A1.VIN
  N7: Raspberry_Pi_1.GPIO6, hc-sr5.Echo
  N8: Raspberry_Pi_1.GPIO13, hc-sr4.Echo
  N9: Raspberry_Pi_1.GPIO19, hc-sr3.Echo
  N10: Raspberry_Pi_1.GPIO26, hc-sr2.Echo
  N11: Raspberry_Pi_1.GPIO21, hc-sr2.Trig
  N12: Raspberry_Pi_1.GPIO20, hc-sr3.Trig
  N13: Raspberry_Pi_1.GPIO16, hc-sr4.Trig
  N14: Raspberry_Pi_1.GPIO12, hc-sr5.Trig
  N15: MD03A1.OUT_1A, M2.pin_1
  N16: MD03A1.OUT_1B, M2.pin_2
  N17: MD03A1.OUT_2A, M1.pin_1
  N18: MD03A1.OUT_2B, M1.pin_2
